# Fritzing sketch Quadcopter_6050 (saved by Fritzing 0.9.3b)
circuit board: 6.88566cm x 5.36311cm
breadboards: 1

parts:
  6 = Basic Servo
  9 = Basic Servo
  10 = Basic Servo
  11 = Basic Servo
  Heavy_v1_0_0_2 = Arduino Uno (Rev3)
  GY2 = MPU-6050 Board GY-521 [form="♀ (female)" package=THT]
  S1 = Pushbutton [package="[THT]"]
  LED1 = LED - 5mm [color="Red (633nm)" package="5 mm [THT]"]
  R1 = Resistor [tolerance=±5% resistance=220 package=THT]
  J0 = female pin header, 2 pins [form="♀ (female)"]
  5 = Basic Servo
  3 = Basic Servo
  J8 = female pin header, 5 pins [form="♀ (female)"]
  3v = female pin header, 2 pins [form="♀ (female)"]
  5v = female pin header, 2 pins [form="♀ (female)"]
  12 = Basic Servo
  8 = Basic Servo
  7 = Basic Servo
  4 = Basic Servo
  2 = Basic Servo
  1 = Basic Servo
  0 = Basic Servo
  J9 = female pin header, 2 pins [form="♀ (female)"]

nets:
  GND: 6.gnd, 9.gnd, 10.gnd, 11.gnd, Heavy_v1_0_0_2.GND, GY2.pin2, S1.Pin_3, S1.Pin_4, R1.Pin_0, 5.gnd, 3.gnd, J8.pin1, 3v.pin1, 5v.pin1, 12.gnd, 8.gnd, 7.gnd, 4.gnd, 2.gnd, 1.gnd, 0.gnd
  N1: 6.pulse, Heavy_v1_0_0_2.D6_PWM
  N2: 9.pulse, Heavy_v1_0_0_2.D9_PWM
  N3: 10.pulse, Heavy_v1_0_0_2.D10_PWM/SS
  N4: 11.vcc, J0.pin1
  N5: 11.pulse, Heavy_v1_0_0_2.D11_PWM/MOSI
  N6: Heavy_v1_0_0_2.A0, J8.pin2
  N7: Heavy_v1_0_0_2.A1, J8.pin3
  N8: Heavy_v1_0_0_2.A2, J8.pin4
  N9: Heavy_v1_0_0_2.A3, J8.pin5
  N10: Heavy_v1_0_0_2.A4/SDA, GY2.pin4
  N11: Heavy_v1_0_0_2.A5/SCL, GY2.pin3
  N12: Heavy_v1_0_0_2.D8, 8.pulse
  N13: Heavy_v1_0_0_2.D12/MISO, 12.pulse
  N14: Heavy_v1_0_0_2.D13/SCK, LED1.anode
  N15: Heavy_v1_0_0_2.D0/RX, 0.pulse
  N16: Heavy_v1_0_0_2.D1/TX, 1.pulse
  N17: Heavy_v1_0_0_2.D2, GY2.pin8, 2.pulse
  N18: Heavy_v1_0_0_2.D3_PWM, 3.pulse
  N19: Heavy_v1_0_0_2.D4, 4.pulse
  N20: Heavy_v1_0_0_2.D5_PWM, 5.pulse
  N21: Heavy_v1_0_0_2.D7, 7.pulse
  N22: Heavy_v1_0_0_2.RESET, S1.Pin_1, S1.Pin_2
  N23: Heavy_v1_0_0_2.3V3, GY2.pin1, 3v.pin2
  N24: Heavy_v1_0_0_2.5V, 5v.pin2
  N25: Heavy_v1_0_0_2.VIN, J0.pin2, J9.pin2
  N26: LED1.cathode, R1.Pin_1
  N27: 3.vcc, J9.pin1

notes:
  amir aliabadi

custom parts:
  MPU-6050 Board GY-521: Acelerometro y Giroscopio MPU-6050 Board GY-521
